// Logisim project EXP_5(Async).circ as structural Verilog: 1 circuit, main circuit main
module main (
  input  in_1,
  input  in_2,
  output out_3,
  output out_4,
  output out_5
);

  wire clock_1_out, clock_2_out, j_k_ff_1_qn, j_k_ff_2_qn, j_k_ff_3_qn;

  Clock clock_1 (.out(clock_1_out));
  Clock clock_2 (.out(clock_2_out));
  J_K_Flip_Flop j_k_ff_1 (
    .J(in_2), .clk(clock_1_out), .K(in_2), .Q(out_4), .Qn(j_k_ff_1_qn));  // open: preset, en, reset
  J_K_Flip_Flop j_k_ff_2 (.J(in_1), .clk(clock_2_out), .K(in_1), .Qn(j_k_ff_2_qn));  // open: Q, preset, en, reset
  J_K_Flip_Flop j_k_ff_3 (
    .J(in_2), .clk(j_k_ff_1_qn), .K(in_2), .Q(out_5), .Qn(j_k_ff_3_qn));  // open: preset, en, reset
  J_K_Flip_Flop j_k_ff_4 (.J(in_1), .clk(j_k_ff_2_qn), .K(in_1), .Q(out_3));  // open: Qn, preset, en, reset
  J_K_Flip_Flop j_k_ff_5 (.J(in_2), .clk(j_k_ff_3_qn), .K(in_2));  // open: Q, Qn, preset, en, reset

  // Notes on the sheet:
  //   2-Bit (MOD 4) Ripple Counter 
  //   3-Bit (MOD 4) Ripple Counter 
endmodule
